# Fritzing sketch Ideal (saved by Fritzing 0.9.6b)

parts:
  LCM1602_IIC1 = LCM1602 IIC [part_number="LCM1602 IIC" chip_label="LCM1602 IIC" package="DIP (Dual Inline) [THT]"]
  Componente1 = Arduino Nano (Rev3.0)
  LCD1 = LCD screen
  U2 = POT [package=pot_alpha_rv16af-20]
  U4 = RELAY-SOLIDSTATE [package=relay-s108t02]
  L1 = Inductor [inductance=10 package="400 mil [THT]"]
  L2 = Inductor [inductance=10 package="400 mil [THT]"]  # not connected
  L3 = Inductor [inductance=10 package="400 mil [THT]"]  # not connected
  L4 = Inductor [inductance=10 package="400 mil [THT]"]  # not connected
  L5 = Inductor [inductance=10 package="400 mil [THT]"]
  L7 = Inductor [inductance=10 package="400 mil [THT]"]  # not connected
  L8 = Inductor [inductance=10 package="400 mil [THT]"]
  L9 = Inductor [inductance=10 package="400 mil [THT]"]  # not connected
  L11 = Inductor [inductance=10 package="400 mil [THT]"]  # not connected
  L12 = Inductor [inductance=10 package="400 mil [THT]"]  # not connected
  U5 = MAX6675 [package=so08]
  S1 = Tilt Switch [package=THT]
  S2 = Momentary Switch [package=ksa_sealed_tac_switch]
  S3 = Momentary Switch [package=ksa_sealed_tac_switch]
  R2 = Resistor [tolerance=±5% power=0.25 resistance=220 package=THT]
  R1 = Resistor [tolerance=±5% power=0.25 resistance=220 package=THT]
  Power_plug1 = Power plug

nets:
  VSS: LCM1602_IIC1.VSS, LCD1.VSS
  VDD: LCM1602_IIC1.VDD, LCD1.VDD
  N1: LCM1602_IIC1.V0, LCD1.V0
  N2: LCM1602_IIC1.RS, LCD1.RS
  N3: LCM1602_IIC1.RW, LCD1.R/W
  N4: LCM1602_IIC1.E, LCD1.E
  N5: LCM1602_IIC1.D0, LCD1.DB0
  N6: LCM1602_IIC1.D1, LCD1.DB1
  N7: LCM1602_IIC1.D2, LCD1.DB2
  N8: LCM1602_IIC1.D3, LCD1.DB3
  N9: LCM1602_IIC1.D4, LCD1.DB4
  N10: LCM1602_IIC1.D5, LCD1.DB5
  N11: LCM1602_IIC1.D6, LCD1.DB6
  N12: LCM1602_IIC1.D7, LCD1.DB7
  N13: LCM1602_IIC1.A, LCD1.LED+
  N14: LCM1602_IIC1.K, LCD1.LED-
  GND: LCM1602_IIC1.GND, Componente1.GND, U2.A, U4.-, U5.VSS, R2.Pin_1, R1.Pin_1, Power_plug1.GND
  VCC: LCM1602_IIC1.VCC, Componente1.5V, U2.E, U5.VDD, S2.3, S3.3
  N15: LCM1602_IIC1.SDA, Componente1.A4
  N16: LCM1602_IIC1.SCL, Componente1.A5
  N17: Componente1.D2, S2.2, R2.Pin_0
  N18: Componente1.D3, S3.2, R1.Pin_0
  N19: Componente1.D4, U5.MISO
  N20: Componente1.D5, U5.CS
  N21: Componente1.D6, U5.SCK
  VIN: Componente1.VIN, Power_plug1.VCC
  N22: Componente1.A7, U2.S
  N23: Componente1.D13/SCK, U4.+
  N24: U4.T1, L5.pin_1
  N25: L1.pin_0, L8.pin_0
  N26: U5.T-, S1.Pin_2
  N27: U5.T+, S1.Pin_1

notes:
  110V
  0V
  5V
  2A

custom parts:
  LCM1602 IIC: I2C-Module to use a 1602 or 2004 LCD on with the wire.h libory Serial LCD Modul
